# Fritzing sketch Main (saved by Fritzing 0.9.3b)
breadboards: 1

parts:
  Part1 = Arduino Nano (Rev3.0)
  R1 = Resistor [tolerance=±5% resistance=1k package=THT]
  C1 = Ceramic Capacitor [capacitance=13pF voltage=6V package="100 mil [THT, multilayer]"]
  R2 = Trimmer Potentiometer [maximum_resistance=10kΩ package=THT]
  C2 = Electrolytic Capacitor [capacitance=22µF package="100 mil [THT, electrolytic]"]
  SPKR1 = Loudspeaker
  R3 = Resistor [tolerance=±5% resistance=1k package=THT]
  U1 = AD22100 - Voltage Output Temperature Sensor with Signal Conditioning [part_number="Hall sensor"]
  R6 = Resistor [tolerance=±5% resistance=330 package=THT]
  LED1 = LED - 5mm [color="Green (555nm)" package="5 mm [THT]"]
  R7 = Resistor [tolerance=±5% resistance=330 package=THT]
  R4 = Trimmer Potentiometer [maximum_resistance=1kΩ package=THT]

nets:
  N1: Part1.GND, C1.0, R2.leg2, SPKR1.pin2, R3.Pin_1
  N2: Part1.D2, U1.V+, R6.Pin_1, R7.Pin_1
  N3: Part1.D11/MOSI, R1.Pin_0
  N4: Part1.5V, R4.leg1
  N5: Part1.A5, R4.wiper
  N6: R1.Pin_1, C1.1, R2.leg1
  N7: R2.wiper, C2.+
  N8: C2.-, SPKR1.pin1
  N9: R3.Pin_0, R4.leg2
  N10: U1.Vo, LED1.cathode
  N11: U1.GND, R6.Pin_0
  N12: LED1.anode, R7.Pin_0
